# Fritzing sketch Scarlet Knights Final PCB (saved by Fritzing 0.9.3b)
circuit board: 5.88109cm x 3.37248cm
breadboards: 1

parts:
  Part1 = Arduino Nano (Rev3.0)
  J1 = female pin header, 5 pins [form="♀ (female)"]
  12v_gnd1 = Terminal 2pin
  J6 = female pin header, 3 pins [form="♀ (female)"]
  J5 = female pin header, 3 pins [form="♀ (female)"]
  J4 = female pin header, 3 pins [form="♀ (female)"]
  J3 = female pin header, 3 pins [form="♀ (female)"]
  J2 = female pin header, 3 pins [form="♀ (female)"]

nets:
  N1: Part1.D2, J3.pin1
  N2: Part1.D3, J2.pin1
  N3: Part1.D4, J4.pin1
  N4: Part1.D5, J5.pin3
  N5: Part1.D6, J6.pin1
  N6: Part1.D9, J1.pin2
  N7: Part1.D10, J1.pin3
  N8: Part1.D11/MOSI, J1.pin4
  N9: Part1.D12/MISO, J1.pin5
  N10: Part1.VIN, 12v_gnd1.pin_1
  N11: Part1.GND, J1.pin1, 12v_gnd1.pin_2, J6.pin2, J5.pin2, J4.pin2, J3.pin2, J2.pin2
  N12: Part1.5V, J6.pin3, J5.pin1, J4.pin3, J3.pin3, J2.pin3

custom parts:
  Terminal 2pin: 2-pin Terminal Block
